// Logisim project hc01.circ as structural Verilog: 26 circuits, main circuit NotGate
module NotGate (
  input  a,
  output nota
);

  nand nand_1 (nota, a, a);
endmodule

module AndGate (
  input  a,
  input  b,
  output aandb
);

  wire nand_1_out;

  nand nand_1 (nand_1_out, a, b);
  nand nand_2 (aandb, nand_1_out, nand_1_out);
endmodule

module OrGate (
  input  a,
  input  b,
  output aorb
);

  wire nand_1_out, nand_2_out;

  nand nand_1 (nand_1_out, a, a);
  nand nand_2 (nand_2_out, b, b);
  nand nand_3 (aorb, nand_1_out, nand_2_out);
endmodule

module XorGate (
  input  a,
  input  b,
  output axorb
);

  wire nand_1_out, nand_2_out, nand_3_out, nand_4_out;

  nand nand_1 (nand_1_out, a, a);
  nand nand_2 (nand_2_out, b, b);
  nand nand_3 (nand_3_out, nand_1_out, b);
  nand nand_4 (nand_4_out, a, nand_2_out);
  nand nand_5 (axorb, nand_3_out, nand_4_out);
endmodule

module MuxGate (
  input  a,
  input  sel,
  input  b,
  output muxab
);

  wire nand_1_out, nand_2_out, nand_3_out;

  nand nand_1 (nand_1_out, sel, sel);
  nand nand_2 (nand_2_out, a, nand_1_out);
  nand nand_3 (nand_3_out, sel, b);
  nand nand_4 (muxab, nand_2_out, nand_3_out);
endmodule

module DMuxGate (
  input  inbit,
  input  sel,
  output a,
  output b
);

  wire nand_1_out, nand_2_out, nand_3_out;

  nand nand_1 (nand_1_out, sel, sel);
  nand nand_2 (nand_2_out, inbit, nand_1_out);
  nand nand_3 (nand_3_out, sel, inbit);
  nand nand_4 (a, nand_2_out, nand_2_out);
  nand nand_5 (b, nand_3_out, nand_3_out);
endmodule

module Not16 (
  input  [15:0] in16bit,
  output [15:0] out16bit
);

  NotGate notgate_1 (.nota(out16bit[0]), .a(in16bit[0]));
  NotGate notgate_2 (.nota(out16bit[1]), .a(in16bit[1]));
  NotGate notgate_3 (.nota(out16bit[2]), .a(in16bit[2]));
  NotGate notgate_4 (.nota(out16bit[3]), .a(in16bit[3]));
  NotGate notgate_5 (.nota(out16bit[4]), .a(in16bit[4]));
  NotGate notgate_6 (.nota(out16bit[5]), .a(in16bit[5]));
  NotGate notgate_7 (.nota(out16bit[6]), .a(in16bit[6]));
  NotGate notgate_8 (.nota(out16bit[7]), .a(in16bit[7]));
  NotGate notgate_9 (.nota(out16bit[8]), .a(in16bit[8]));
  NotGate notgate_10 (.nota(out16bit[9]), .a(in16bit[9]));
  NotGate notgate_11 (.nota(out16bit[10]), .a(in16bit[10]));
  NotGate notgate_12 (.nota(out16bit[11]), .a(in16bit[11]));
  NotGate notgate_13 (.nota(out16bit[12]), .a(in16bit[12]));
  NotGate notgate_14 (.nota(out16bit[13]), .a(in16bit[13]));
  NotGate notgate_15 (.nota(out16bit[14]), .a(in16bit[14]));
  NotGate notgate_16 (.nota(out16bit[15]), .a(in16bit[15]));
endmodule

module And16 (
  input  [15:0] a,
  input  [15:0] b,
  output [15:0] aANDb
);

  AndGate andgate_1 (.aandb(aANDb[0]), .b(b[0]), .a(a[0]));
  AndGate andgate_2 (.aandb(aANDb[1]), .b(b[1]), .a(a[1]));
  AndGate andgate_3 (.aandb(aANDb[2]), .b(b[2]), .a(a[2]));
  AndGate andgate_4 (.aandb(aANDb[3]), .b(b[3]), .a(a[3]));
  AndGate andgate_5 (.aandb(aANDb[4]), .b(b[4]), .a(a[4]));
  AndGate andgate_6 (.aandb(aANDb[5]), .b(b[5]), .a(a[5]));
  AndGate andgate_7 (.aandb(aANDb[6]), .b(b[6]), .a(a[6]));
  AndGate andgate_8 (.aandb(aANDb[7]), .b(b[7]), .a(a[7]));
  AndGate andgate_9 (.aandb(aANDb[8]), .b(b[8]), .a(a[8]));
  AndGate andgate_10 (.aandb(aANDb[9]), .b(b[9]), .a(a[9]));
  AndGate andgate_11 (.aandb(aANDb[10]), .b(b[10]), .a(a[10]));
  AndGate andgate_12 (.aandb(aANDb[11]), .b(b[11]), .a(a[11]));
  AndGate andgate_13 (.aandb(aANDb[12]), .b(b[12]), .a(a[12]));
  AndGate andgate_14 (.aandb(aANDb[13]), .b(b[13]), .a(a[13]));
  AndGate andgate_15 (.aandb(aANDb[14]), .b(b[14]), .a(a[14]));
  AndGate andgate_16 (.aandb(aANDb[15]), .b(b[15]), .a(a[15]));
endmodule

module Or16 (
  input  [15:0] a,
  input  [15:0] b,
  output [15:0] aORb
);

  OrGate orgate_1 (.aorb(aORb[0]), .b(b[0]), .a(a[0]));
  OrGate orgate_2 (.aorb(aORb[1]), .b(b[1]), .a(a[1]));
  OrGate orgate_3 (.aorb(aORb[2]), .b(b[2]), .a(a[2]));
  OrGate orgate_4 (.aorb(aORb[3]), .b(b[3]), .a(a[3]));
  OrGate orgate_5 (.aorb(aORb[4]), .b(b[4]), .a(a[4]));
  OrGate orgate_6 (.aorb(aORb[5]), .b(b[5]), .a(a[5]));
  OrGate orgate_7 (.aorb(aORb[6]), .b(b[6]), .a(a[6]));
  OrGate orgate_8 (.aorb(aORb[7]), .b(b[7]), .a(a[7]));
  OrGate orgate_9 (.aorb(aORb[8]), .b(b[8]), .a(a[8]));
  OrGate orgate_10 (.aorb(aORb[9]), .b(b[9]), .a(a[9]));
  OrGate orgate_11 (.aorb(aORb[10]), .b(b[10]), .a(a[10]));
  OrGate orgate_12 (.aorb(aORb[11]), .b(b[11]), .a(a[11]));
  OrGate orgate_13 (.aorb(aORb[12]), .b(b[12]), .a(a[12]));
  OrGate orgate_14 (.aorb(aORb[13]), .b(b[13]), .a(a[13]));
  OrGate orgate_15 (.aorb(aORb[14]), .b(b[14]), .a(a[14]));
  OrGate orgate_16 (.aorb(aORb[15]), .b(b[15]), .a(a[15]));
endmodule

module Mux16 (
  input  sel,
  input  [15:0] a,
  input  [15:0] b,
  output [15:0] abMUX
);

  MuxGate muxgate_1 (.muxab(abMUX[0]), .sel(sel), .b(b[0]), .a(a[0]));
  MuxGate muxgate_2 (.muxab(abMUX[1]), .sel(sel), .b(b[1]), .a(a[1]));
  MuxGate muxgate_3 (.muxab(abMUX[2]), .sel(sel), .b(b[2]), .a(a[2]));
  MuxGate muxgate_4 (.muxab(abMUX[3]), .sel(sel), .b(b[3]), .a(a[3]));
  MuxGate muxgate_5 (.muxab(abMUX[4]), .sel(sel), .b(b[4]), .a(a[4]));
  MuxGate muxgate_6 (.muxab(abMUX[5]), .sel(sel), .b(b[5]), .a(a[5]));
  MuxGate muxgate_7 (.muxab(abMUX[6]), .sel(sel), .b(b[6]), .a(a[6]));
  MuxGate muxgate_8 (.muxab(abMUX[7]), .sel(sel), .b(b[7]), .a(a[7]));
  MuxGate muxgate_9 (.muxab(abMUX[8]), .sel(sel), .b(b[8]), .a(a[8]));
  MuxGate muxgate_10 (.muxab(abMUX[9]), .sel(sel), .b(b[9]), .a(a[9]));
  MuxGate muxgate_11 (.muxab(abMUX[10]), .sel(sel), .b(b[10]), .a(a[10]));
  MuxGate muxgate_12 (.muxab(abMUX[11]), .sel(sel), .b(b[11]), .a(a[11]));
  MuxGate muxgate_13 (.muxab(abMUX[12]), .sel(sel), .b(b[12]), .a(a[12]));
  MuxGate muxgate_14 (.muxab(abMUX[13]), .sel(sel), .b(b[13]), .a(a[13]));
  MuxGate muxgate_15 (.muxab(abMUX[14]), .sel(sel), .b(b[14]), .a(a[14]));
  MuxGate muxgate_16 (.muxab(abMUX[15]), .sel(sel), .b(b[15]), .a(a[15]));
endmodule

module Or8Way (
  input  [7:0] in8bit,
  output outOR8WAY
);

  wire orgate_1_aorb, orgate_2_aorb, orgate_3_aorb, orgate_4_aorb, orgate_5_aorb, orgate_6_aorb;

  OrGate orgate_1 (.aorb(orgate_1_aorb), .b(in8bit[1]), .a(in8bit[0]));
  OrGate orgate_2 (.aorb(orgate_2_aorb), .b(in8bit[2]), .a(orgate_1_aorb));
  OrGate orgate_3 (.aorb(orgate_3_aorb), .b(in8bit[3]), .a(orgate_2_aorb));
  OrGate orgate_4 (.aorb(orgate_4_aorb), .b(in8bit[4]), .a(orgate_3_aorb));
  OrGate orgate_5 (.aorb(orgate_5_aorb), .b(in8bit[5]), .a(orgate_4_aorb));
  OrGate orgate_6 (.aorb(orgate_6_aorb), .b(in8bit[6]), .a(orgate_5_aorb));
  OrGate orgate_7 (.aorb(outOR8WAY), .b(in8bit[7]), .a(orgate_6_aorb));
endmodule

module Mux4Way16 (
  input  [1:0] sel,
  input  [15:0] a,
  input  [15:0] b,
  input  [15:0] c,
  input  [15:0] d,
  output [15:0] outMux4Way16
);

  wire [15:0] mux16_1_abmux, mux16_2_abmux;

  Mux16 mux16_1 (.abMUX(mux16_1_abmux), .b(b), .a(a), .sel(sel[0]));
  Mux16 mux16_2 (.abMUX(mux16_2_abmux), .b(d), .a(c), .sel(sel[0]));
  Mux16 mux16_3 (.abMUX(outMux4Way16), .b(mux16_2_abmux), .a(mux16_1_abmux), .sel(sel[1]));
endmodule

module Mux8Way16 (
  input  [2:0] sel,
  input  [15:0] a,
  input  [15:0] b,
  input  [15:0] c,
  input  [15:0] d,
  input  [15:0] e,
  input  [15:0] f,
  input  [15:0] g,
  input  [15:0] h,
  output [15:0] outMux8Way16
);

  wire [15:0] mux4way16_1_outmux4way16, mux4way16_2_outmux4way16;

  Mux4Way16 mux4way16_1 (.outMux4Way16(mux4way16_1_outmux4way16), .b(b), .c(c), .d(d), .a(a), .sel(sel[1:0]));
  Mux4Way16 mux4way16_2 (.outMux4Way16(mux4way16_2_outmux4way16), .b(f), .c(g), .d(h), .a(e), .sel(sel[1:0]));
  Mux16 mux16_1 (.abMUX(outMux8Way16), .b(mux4way16_2_outmux4way16), .a(mux4way16_1_outmux4way16), .sel(sel[2]));
endmodule

module DMux4Way (
  input  [1:0] sel,
  input  inBit,
  output a,
  output c,
  output b,
  output d
);

  wire dmuxgate_1_a, dmuxgate_1_b;

  DMuxGate dmuxgate_1 (.a(dmuxgate_1_a), .b(dmuxgate_1_b), .inbit(inBit), .sel(sel[0]));
  DMuxGate dmuxgate_2 (.a(a), .b(c), .inbit(dmuxgate_1_a), .sel(sel[1]));
  DMuxGate dmuxgate_3 (.a(b), .b(d), .inbit(dmuxgate_1_b), .sel(sel[1]));
endmodule

module DMux8Way (
  input  [2:0] sel,
  input  inBit,
  output a,
  output c,
  output e,
  output g,
  output b,
  output d,
  output f,
  output h
);

  wire dmuxgate_1_a, dmuxgate_1_b;

  DMuxGate dmuxgate_1 (.a(dmuxgate_1_a), .b(dmuxgate_1_b), .inbit(inBit), .sel(sel[0]));
  DMux4Way dmux4way_1 (.a(a), .c(e), .b(c), .d(g), .inBit(dmuxgate_1_a), .sel(sel[2:1]));
  DMux4Way dmux4way_2 (.a(b), .c(f), .b(d), .d(h), .inBit(dmuxgate_1_b), .sel(sel[2:1]));
endmodule

module HalfAdder (
  input  a,
  input  b,
  output sum,
  output carry
);

  XorGate xorgate_1 (.axorb(sum), .b(b), .a(a));
  AndGate andgate_1 (.aandb(carry), .b(b), .a(a));
endmodule

module FullAdder (
  input  a,
  input  b,
  input  c,
  output sum,
  output carry
);

  wire halfadder_1_carry, halfadder_1_sum, halfadder_2_carry;

  HalfAdder halfadder_1 (.sum(halfadder_1_sum), .carry(halfadder_1_carry), .b(b), .a(a));
  HalfAdder halfadder_2 (.sum(sum), .carry(halfadder_2_carry), .b(c), .a(halfadder_1_sum));
  OrGate orgate_1 (.aorb(carry), .b(halfadder_1_carry), .a(halfadder_2_carry));
endmodule

module Add16 (
  input  [15:0] a,
  input  [15:0] b,
  output [15:0] sum
);

  wire fulladder_2_carry, fulladder_3_carry, fulladder_4_carry, fulladder_5_carry, fulladder_6_carry,
       fulladder_7_carry, fulladder_8_carry, fulladder_9_carry, fulladder_10_carry, fulladder_11_carry,
       fulladder_12_carry, fulladder_13_carry, fulladder_14_carry, fulladder_15_carry, halfadder_1_carry;

  FullAdder fulladder_1 (.sum(sum[15]), .b(b[15]), .c(fulladder_2_carry), .a(a[15]));  // open: carry
  FullAdder fulladder_2 (.carry(fulladder_2_carry), .sum(sum[14]), .b(b[14]), .c(fulladder_3_carry), .a(a[14]));
  FullAdder fulladder_3 (.carry(fulladder_3_carry), .sum(sum[13]), .b(b[13]), .c(fulladder_4_carry), .a(a[13]));
  FullAdder fulladder_4 (.carry(fulladder_4_carry), .sum(sum[12]), .b(b[12]), .c(fulladder_5_carry), .a(a[12]));
  FullAdder fulladder_5 (.carry(fulladder_5_carry), .sum(sum[11]), .b(b[11]), .c(fulladder_6_carry), .a(a[11]));
  FullAdder fulladder_6 (.carry(fulladder_6_carry), .sum(sum[10]), .b(b[10]), .c(fulladder_7_carry), .a(a[10]));
  FullAdder fulladder_7 (.carry(fulladder_7_carry), .sum(sum[9]), .b(b[9]), .c(fulladder_8_carry), .a(a[9]));
  FullAdder fulladder_8 (.carry(fulladder_8_carry), .sum(sum[8]), .b(b[8]), .c(fulladder_9_carry), .a(a[8]));
  FullAdder fulladder_9 (.carry(fulladder_9_carry), .sum(sum[7]), .b(b[7]), .c(fulladder_10_carry), .a(a[7]));
  FullAdder fulladder_10 (.carry(fulladder_10_carry), .sum(sum[6]), .b(b[6]), .c(fulladder_11_carry), .a(a[6]));
  FullAdder fulladder_11 (.carry(fulladder_11_carry), .sum(sum[5]), .b(b[5]), .c(fulladder_12_carry), .a(a[5]));
  FullAdder fulladder_12 (.carry(fulladder_12_carry), .sum(sum[4]), .b(b[4]), .c(fulladder_13_carry), .a(a[4]));
  FullAdder fulladder_13 (.carry(fulladder_13_carry), .sum(sum[3]), .b(b[3]), .c(fulladder_14_carry), .a(a[3]));
  FullAdder fulladder_14 (.carry(fulladder_14_carry), .sum(sum[2]), .b(b[2]), .c(fulladder_15_carry), .a(a[2]));
  FullAdder fulladder_15 (.carry(fulladder_15_carry), .sum(sum[1]), .b(b[1]), .c(halfadder_1_carry), .a(a[1]));
  HalfAdder halfadder_1 (.sum(sum[0]), .carry(halfadder_1_carry), .b(b[0]), .a(a[0]));
endmodule

module Inc16 (
  input  [15:0] in16Bit,
  output [15:0] out16Bit
);

  wire notgate_2_nota, notgate_3_nota, notgate_4_nota, notgate_5_nota, notgate_6_nota, notgate_7_nota,
       notgate_8_nota, notgate_9_nota, notgate_10_nota, notgate_11_nota, notgate_12_nota, notgate_13_nota,
       notgate_14_nota, notgate_15_nota, notgate_16_nota, orgate_1_aorb, orgate_2_aorb, orgate_3_aorb,
       orgate_4_aorb, orgate_5_aorb, orgate_6_aorb, orgate_7_aorb, orgate_8_aorb, orgate_9_aorb,
       orgate_10_aorb, orgate_11_aorb, orgate_12_aorb, orgate_13_aorb, orgate_14_aorb;

  NotGate notgate_1 (.nota(out16Bit[0]), .a(in16Bit[0]));
  NotGate notgate_2 (.nota(notgate_2_nota), .a(in16Bit[1]));
  NotGate notgate_3 (.nota(notgate_3_nota), .a(in16Bit[2]));
  NotGate notgate_4 (.nota(notgate_4_nota), .a(in16Bit[3]));
  NotGate notgate_5 (.nota(notgate_5_nota), .a(in16Bit[4]));
  NotGate notgate_6 (.nota(notgate_6_nota), .a(in16Bit[5]));
  NotGate notgate_7 (.nota(notgate_7_nota), .a(in16Bit[6]));
  NotGate notgate_8 (.nota(notgate_8_nota), .a(in16Bit[7]));
  NotGate notgate_9 (.nota(notgate_9_nota), .a(in16Bit[8]));
  NotGate notgate_10 (.nota(notgate_10_nota), .a(in16Bit[9]));
  NotGate notgate_11 (.nota(notgate_11_nota), .a(in16Bit[10]));
  NotGate notgate_12 (.nota(notgate_12_nota), .a(in16Bit[11]));
  NotGate notgate_13 (.nota(notgate_13_nota), .a(in16Bit[12]));
  NotGate notgate_14 (.nota(notgate_14_nota), .a(in16Bit[13]));
  NotGate notgate_15 (.nota(notgate_15_nota), .a(in16Bit[14]));
  NotGate notgate_16 (.nota(notgate_16_nota), .a(in16Bit[15]));
  MuxGate muxgate_1 (.muxab(out16Bit[1]), .sel(out16Bit[0]), .b(in16Bit[1]), .a(notgate_2_nota));
  MuxGate muxgate_2 (.muxab(out16Bit[2]), .sel(orgate_1_aorb), .b(in16Bit[2]), .a(notgate_3_nota));
  MuxGate muxgate_3 (.muxab(out16Bit[3]), .sel(orgate_2_aorb), .b(in16Bit[3]), .a(notgate_4_nota));
  MuxGate muxgate_4 (.muxab(out16Bit[4]), .sel(orgate_3_aorb), .b(in16Bit[4]), .a(notgate_5_nota));
  MuxGate muxgate_5 (.muxab(out16Bit[5]), .sel(orgate_4_aorb), .b(in16Bit[5]), .a(notgate_6_nota));
  MuxGate muxgate_6 (.muxab(out16Bit[6]), .sel(orgate_5_aorb), .b(in16Bit[6]), .a(notgate_7_nota));
  MuxGate muxgate_7 (.muxab(out16Bit[7]), .sel(orgate_6_aorb), .b(in16Bit[7]), .a(notgate_8_nota));
  MuxGate muxgate_8 (.muxab(out16Bit[8]), .sel(orgate_7_aorb), .b(in16Bit[8]), .a(notgate_9_nota));
  MuxGate muxgate_9 (.muxab(out16Bit[9]), .sel(orgate_8_aorb), .b(in16Bit[9]), .a(notgate_10_nota));
  MuxGate muxgate_10 (.muxab(out16Bit[10]), .sel(orgate_9_aorb), .b(in16Bit[10]), .a(notgate_11_nota));
  MuxGate muxgate_11 (.muxab(out16Bit[11]), .sel(orgate_10_aorb), .b(in16Bit[11]), .a(notgate_12_nota));
  MuxGate muxgate_12 (.muxab(out16Bit[12]), .sel(orgate_11_aorb), .b(in16Bit[12]), .a(notgate_13_nota));
  MuxGate muxgate_13 (.muxab(out16Bit[13]), .sel(orgate_12_aorb), .b(in16Bit[13]), .a(notgate_14_nota));
  MuxGate muxgate_14 (.muxab(out16Bit[14]), .sel(orgate_13_aorb), .b(in16Bit[14]), .a(notgate_15_nota));
  MuxGate muxgate_15 (.muxab(out16Bit[15]), .sel(orgate_14_aorb), .b(in16Bit[15]), .a(notgate_16_nota));
  OrGate orgate_1 (.aorb(orgate_1_aorb), .b(notgate_2_nota), .a(out16Bit[1]));
  OrGate orgate_2 (.aorb(orgate_2_aorb), .b(notgate_3_nota), .a(out16Bit[2]));
  OrGate orgate_3 (.aorb(orgate_3_aorb), .b(notgate_4_nota), .a(out16Bit[3]));
  OrGate orgate_4 (.aorb(orgate_4_aorb), .b(notgate_5_nota), .a(out16Bit[4]));
  OrGate orgate_5 (.aorb(orgate_5_aorb), .b(notgate_6_nota), .a(out16Bit[5]));
  OrGate orgate_6 (.aorb(orgate_6_aorb), .b(notgate_7_nota), .a(out16Bit[6]));
  OrGate orgate_7 (.aorb(orgate_7_aorb), .b(notgate_8_nota), .a(out16Bit[7]));
  OrGate orgate_8 (.aorb(orgate_8_aorb), .b(notgate_9_nota), .a(out16Bit[8]));
  OrGate orgate_9 (.aorb(orgate_9_aorb), .b(notgate_10_nota), .a(out16Bit[9]));
  OrGate orgate_10 (.aorb(orgate_10_aorb), .b(notgate_11_nota), .a(out16Bit[10]));
  OrGate orgate_11 (.aorb(orgate_11_aorb), .b(notgate_12_nota), .a(out16Bit[11]));
  OrGate orgate_12 (.aorb(orgate_12_aorb), .b(notgate_13_nota), .a(out16Bit[12]));
  OrGate orgate_13 (.aorb(orgate_13_aorb), .b(notgate_14_nota), .a(out16Bit[13]));
  OrGate orgate_14 (.aorb(orgate_14_aorb), .b(notgate_15_nota), .a(out16Bit[14]));
endmodule

module ALU (
  input  zx,
  input  nx,
  input  zy,
  input  ny,
  input  f,
  input  no,
  input  [15:0] x,
  input  [15:0] y,
  output [15:0] outALU,
  output zr,
  output ng
);

  wire or8way_1_outor8way, or8way_2_outor8way, orgate_1_aorb;
  wire [15:0] add16_1_sum, and16_1_aandb, mux16_1_abmux, mux16_2_abmux, mux16_3_abmux, mux16_4_abmux,
       mux16_5_abmux, not16_1_out16bit, not16_2_out16bit, not16_3_out16bit;

  Mux16 mux16_1 (.abMUX(mux16_1_abmux), .b({16{1'b0}}), .a(x), .sel(zx));
  Not16 not16_1 (.out16bit(not16_1_out16bit), .in16bit(mux16_1_abmux));
  Mux16 mux16_2 (.abMUX(mux16_2_abmux), .b(not16_1_out16bit), .a(mux16_1_abmux), .sel(nx));
  Mux16 mux16_3 (.abMUX(mux16_3_abmux), .b({16{1'b0}}), .a(y), .sel(zy));
  Mux16 mux16_4 (.abMUX(mux16_4_abmux), .b(not16_2_out16bit), .a(mux16_3_abmux), .sel(ny));
  Not16 not16_2 (.out16bit(not16_2_out16bit), .in16bit(mux16_3_abmux));
  And16 and16_1 (.aANDb(and16_1_aandb), .b(mux16_4_abmux), .a(mux16_2_abmux));
  Add16 add16_1 (.sum(add16_1_sum), .a(mux16_2_abmux), .b(mux16_4_abmux));
  Mux16 mux16_5 (.abMUX(mux16_5_abmux), .b(add16_1_sum), .a(and16_1_aandb), .sel(f));
  Not16 not16_3 (.out16bit(not16_3_out16bit), .in16bit(mux16_5_abmux));
  Mux16 mux16_6 (.abMUX({ng, outALU[14:0]}), .b(not16_3_out16bit), .a(mux16_5_abmux), .sel(no));
  Or8Way or8way_1 (.outOR8WAY(or8way_1_outor8way), .in8bit({ng, outALU[14:8]}));
  Or8Way or8way_2 (.outOR8WAY(or8way_2_outor8way), .in8bit(outALU[7:0]));
  OrGate orgate_1 (.aorb(orgate_1_aorb), .b(or8way_1_outor8way), .a(or8way_2_outor8way));
  NotGate notgate_1 (.nota(zr), .a(orgate_1_aorb));

  assign outALU[15] = ng;
endmodule

module Bit (
  input  load,
  input  inBit,
  output outBit
);

  wire clock_1_out, muxgate_1_muxab;

  MuxGate muxgate_1 (.muxab(muxgate_1_muxab), .sel(load), .b(inBit), .a(outBit));
  Clock clock_1 (.out(clock_1_out));
  D_Flip_Flop d_ff_1 (.D(muxgate_1_muxab), .clk(clock_1_out), .Q(outBit));  // open: Qn, preset, reset
endmodule

module RegisterCircuit (
  input  load,
  input  [15:0] in16,
  output [15:0] out16
);

  Bit bit_1 (.outBit(out16[0]), .inBit(in16[0]), .load(load));
  Bit bit_2 (.outBit(out16[1]), .inBit(in16[1]), .load(load));
  Bit bit_3 (.outBit(out16[2]), .inBit(in16[2]), .load(load));
  Bit bit_4 (.outBit(out16[3]), .inBit(in16[3]), .load(load));
  Bit bit_5 (.outBit(out16[4]), .inBit(in16[4]), .load(load));
  Bit bit_6 (.outBit(out16[5]), .inBit(in16[5]), .load(load));
  Bit bit_7 (.outBit(out16[6]), .inBit(in16[6]), .load(load));
  Bit bit_8 (.outBit(out16[7]), .inBit(in16[7]), .load(load));
  Bit bit_9 (.outBit(out16[8]), .inBit(in16[8]), .load(load));
  Bit bit_10 (.outBit(out16[9]), .inBit(in16[9]), .load(load));
  Bit bit_11 (.outBit(out16[10]), .inBit(in16[10]), .load(load));
  Bit bit_12 (.outBit(out16[11]), .inBit(in16[11]), .load(load));
  Bit bit_13 (.outBit(out16[12]), .inBit(in16[12]), .load(load));
  Bit bit_14 (.outBit(out16[13]), .inBit(in16[13]), .load(load));
  Bit bit_15 (.outBit(out16[14]), .inBit(in16[14]), .load(load));
  Bit bit_16 (.outBit(out16[15]), .inBit(in16[15]), .load(load));
endmodule

module RAM8 (
  input  [2:0] address,
  input  [15:0] in16,
  input  load,
  output [15:0] out16
);

  wire dmux8way_1_a, dmux8way_1_b, dmux8way_1_c, dmux8way_1_d, dmux8way_1_e, dmux8way_1_f, dmux8way_1_g,
       dmux8way_1_h;
  wire [15:0] registercircuit_1_out16, registercircuit_2_out16, registercircuit_3_out16,
       registercircuit_4_out16, registercircuit_5_out16, registercircuit_6_out16, registercircuit_7_out16,
       registercircuit_8_out16;

  DMux8Way dmux8way_1 (
    .e(dmux8way_1_e), .g(dmux8way_1_g), .b(dmux8way_1_b), .d(dmux8way_1_d), .f(dmux8way_1_f),
    .h(dmux8way_1_h), .a(dmux8way_1_a), .c(dmux8way_1_c), .sel(address), .inBit(load));
  RegisterCircuit registercircuit_1 (.out16(registercircuit_1_out16), .in16(in16), .load(dmux8way_1_a));
  RegisterCircuit registercircuit_2 (.out16(registercircuit_2_out16), .in16(in16), .load(dmux8way_1_b));
  RegisterCircuit registercircuit_3 (.out16(registercircuit_3_out16), .in16(in16), .load(dmux8way_1_c));
  RegisterCircuit registercircuit_4 (.out16(registercircuit_4_out16), .in16(in16), .load(dmux8way_1_d));
  RegisterCircuit registercircuit_5 (.out16(registercircuit_5_out16), .in16(in16), .load(dmux8way_1_e));
  RegisterCircuit registercircuit_6 (.out16(registercircuit_6_out16), .in16(in16), .load(dmux8way_1_f));
  RegisterCircuit registercircuit_7 (.out16(registercircuit_7_out16), .in16(in16), .load(dmux8way_1_g));
  RegisterCircuit registercircuit_8 (.out16(registercircuit_8_out16), .in16(in16), .load(dmux8way_1_h));
  Mux8Way16 mux8way16_1 (
    .outMux8Way16(out16), .b(registercircuit_2_out16), .c(registercircuit_3_out16),
    .d(registercircuit_4_out16), .e(registercircuit_5_out16), .f(registercircuit_6_out16),
    .g(registercircuit_7_out16), .h(registercircuit_8_out16), .a(registercircuit_1_out16), .sel(address));
endmodule

module RAM64 (
);

  RAM8 ram8_1 ();  // open: out16, load, address, in16
  RAM8 ram8_2 ();  // open: out16, load, address, in16
  RAM8 ram8_3 ();  // open: out16, load, address, in16
  RAM8 ram8_4 ();  // open: out16, load, address, in16
endmodule

module CPU (
  input  [15:0] instruction,
  input  [15:0] inM,
  input  reset,
  output [15:0] outM,
  output writeM,
  output [15:0] addressM,
  output [15:0] pc
);

  wire nand_1_out, or_1_out;
  wire [15:0] D_Reg_out16, mux16_1_abmux, mux16_2_abmux;

  nand nand_1 (nand_1_out, instruction[15], instruction[15]);
  Mux16 mux16_1 (.abMUX(mux16_1_abmux), .b(instruction), .a(outM), .sel(nand_1_out));
  or or_1 (or_1_out, instruction[5], nand_1_out);
  RegisterCircuit A_Reg (.out16(addressM), .in16(mux16_1_abmux), .load(or_1_out));
  Mux16 mux16_2 (.abMUX(mux16_2_abmux), .b(inM), .a(addressM), .sel(instruction[12]));
  ProgramCounter programcounter_1 (.out_PC(pc), .in_PC(addressM), .reset(reset));  // open: inc, load
  RegisterCircuit D_Reg (.out16(D_Reg_out16), .in16(outM), .load(instruction[4]));
  ALU alu_1 (
    .outALU(outM), .x(D_Reg_out16), .y(mux16_2_abmux), .zx(instruction[6]), .nx(instruction[7]),
    .zy(instruction[8]), .ny(instruction[9]), .f(instruction[10]), .no(instruction[11]));  // open: zr, ng

  assign writeM = instruction[3];
endmodule

module ProgramCounter (
  input  inc,
  input  load,
  input  reset,
  input  [15:0] in_PC,
  output [15:0] out_PC
);

  wire orgate_1_aorb, orgate_2_aorb;
  wire [15:0] inc16_1_out16bit, mux16_1_abmux, mux16_2_abmux, mux16_3_abmux;

  Mux16 mux16_1 (.abMUX(mux16_1_abmux), .b(inc16_1_out16bit), .a(out_PC), .sel(inc));
  Mux16 mux16_2 (.abMUX(mux16_2_abmux), .b(in_PC), .a(mux16_1_abmux), .sel(load));
  Mux16 mux16_3 (.abMUX(mux16_3_abmux), .b({16{1'b0}}), .a(mux16_2_abmux), .sel(reset));
  OrGate orgate_1 (.aorb(orgate_1_aorb), .b(inc), .a(load));
  OrGate orgate_2 (.aorb(orgate_2_aorb), .b(orgate_1_aorb), .a(reset));
  RegisterCircuit registercircuit_1 (.out16(out_PC), .in16(mux16_3_abmux), .load(orgate_2_aorb));
  Inc16 inc16_1 (.out16Bit(inc16_1_out16bit), .in16Bit(out_PC));
endmodule
